# Fritzing sketch Drone_JoyStick (saved by Fritzing 1.0.2b)

parts:
  Part1 = Thumb Joystick
  U1 = Nanit [package=_]
  U2 = Adapter Nanit [package=rf24g-2x5]
  Part2 = Thumb Joystick
  U3 = Adapter Nanit [package=rf24g-2x5]

nets:
  GND: Part1.GND, U2.GND
  N1: Part1.HORZ, U2.3
  N2: Part1.VERT, U2.2
  VCC: Part1.VCC, U2.VCC
  N3: U1.Port_#6, U2.Port
  N4: U1.Port_#7, U3.Port
  GND_2: Part2.GND, U3.GND
  N5: Part2.HORZ, U3.2
  N6: Part2.VERT, U3.1
  VCC_2: Part2.VCC, U3.VCC

custom parts:
  Nanit: Nanit 3.4
  Adapter Nanit: Adapter
